# Fritzing sketch Buzzer-Sketch (saved by Fritzing 0.9.2b)
breadboards: 1

parts:
  Raspberry_Pi1 = Raspberry Pi 2
  R3 = Resistor [tolerance=±5% resistance=1k package=THT]
  J1 = Piezo Speaker

nets:
  N1: Raspberry_Pi1.GPIO13, R3.Pin_0
  N2: Raspberry_Pi1.GND, J1.pin1
  N3: R3.Pin_1, J1.pin2
