# Fritzing sketch LEDs-Sketch (saved by Fritzing 0.9.2b)
breadboards: 1

parts:
  Raspberry_Pi1 = Raspberry Pi 2
  LED2 = LED - 5mm [color="Yellow (595nm)" package="5 mm [THT]"]
  R2 = Resistor [tolerance=±5% resistance=470 package=THT]
  R3 = Resistor [tolerance=±5% resistance=470 package=THT]
  R4 = Resistor [tolerance=±5% resistance=470 package=THT]
  LED7 = LED - 5mm [color="Green (570nm)" package="5 mm [THT]"]
  LED6 = LED - 5mm [color="Red (635nm)" package="5 mm [THT]"]

nets:
  N1: Raspberry_Pi1.GPIO26, R2.Pin_0
  N2: Raspberry_Pi1.GPIO21, R4.Pin_0
  N3: Raspberry_Pi1.GPIO20, R3.Pin_0
  N4: Raspberry_Pi1.GND, LED2.cathode, LED7.cathode, LED6.cathode
  N5: LED2.anode, R3.Pin_1
  N6: R2.Pin_1, LED6.anode
  N7: R4.Pin_1, LED7.anode
