# Fritzing sketch l293d-Sketch (saved by Fritzing 0.9.2b)
breadboards: 1

parts:
  Raspberry_Pi1 = Raspberry Pi 2
  M1 = DC Motor
  IC1 = L293D [package=THT]
  VCC1 = 4 x AAA Battery Mount

nets:
  N1: Raspberry_Pi1.GPIO17, IC1.In_1
  N2: Raspberry_Pi1.GPIO27, IC1.In_2
  N3: Raspberry_Pi1.GPIO18, IC1.Enable_1
  N4: Raspberry_Pi1.5V, IC1.0V, IC1.+V, VCC1.-
  N5: M1.pin_1, IC1.Out_2_(_Controlled_by_Enable_1_)
  N6: M1.pin_2, IC1.Out_1_(_Controlled_by_Enable_1_)
  N7: IC1.+Vmotor, VCC1.+
